# Fritzing sketch arduino_mega_xbee (saved by Fritzing 0.9.4)

parts:
  Part2 = XBee Pro RF module
  Part3 = Arduino Mega 2560 (Rev3)

nets:
  VCC: Part2.VCC, Part3.3V3
  N1: Part2.DOUT, Part3.D15/RX3
  N2: Part2.DIN, Part3.D14/TX3
  GND: Part2.GND, Part3.GND
