# Fritzing sketch arduino_uno_nrf24 (saved by Fritzing 0.9.4)

parts:
  Part1 = NRF24L01+ Breakout Board
  Part2 = Arduino Uno (Rev3)

nets:
  GND: Part1.GND, Part2.GND
  VCC: Part1.VCC, Part2.3V3
  N1: Part1.CE, Part2.D7
  N2: Part1.CS, Part2.D8
  N3: Part1.SCK, Part2.D12/MISO
  N4: Part1.MOSI, Part2.D11_PWM/MOSI
  N5: Part1.MISO, Part2.D13/SCK
